// Logisim project TP01.circ as structural Verilog: 1 circuit, main circuit main
module main (
  input  W,
  input  X,
  input  Y,
  input  Z,
  output Output
);

  wire nand_1_out, nand_2_out, nand_3_out, nand_4_out, not_1_out, not_2_out;

  not not_1 (not_1_out, X);
  not not_2 (not_2_out, Z);
  nand nand_1 (nand_1_out, W, not_1_out);
  nand nand_2 (nand_2_out, W, Y);
  nand nand_3 (nand_3_out, W, not_2_out);
  nand nand_4 (nand_4_out, X, not_2_out);
  nand nand_5 (Output, nand_1_out, nand_2_out, nand_3_out, nand_4_out);
endmodule
