// Logisim project circuito.circ as structural Verilog
module main (
  input  in_1,
  input  in_2,
  input  in_3,
  input  in_4,
  input  in_5,
  input  in_6,
  input  in_7,
  input  in_8,
  input  in_9,
  input  in_10,
  input  in_11,
  input  in_12,
  input  in_13,
  input  in_14,
  input  in_15,
  input  in_16,
  input  in_17,
  input  in_18,
  input  in_19,
  input  in_20,
  input  in_21,
  input  in_22,
  input  in_23,
  input  in_24,
  input  in_25,
  input  in_26,
  input  in_27,
  input  in_28,
  input  in_29,
  input  in_30,
  input  in_31,
  input  in_32
);

  wire AZUL_2_s1, AZUL_2_s2, AZUL_2_s3, AZUL_3_s1, AZUL_3_s2, AZUL_3_s3, AZUL_s1, AZUL_s2, AZUL_s3,
       codificador_bin_bcd_1_c0, codificador_bin_bcd_1_c1, codificador_bin_bcd_1_c2,
       codificador_bin_bcd_1_c3, codificador_bin_bcd_1_c4, codificador_bin_bcd_2_c0,
       codificador_bin_bcd_2_c1, codificador_bin_bcd_2_c2, codificador_bin_bcd_2_c3,
       codificador_bin_bcd_2_c4, comparador_4_bits_1_a_b, comparador_4_bits_1_a_b_2,
       comparador_4_bits_1_a_b_3, n4_7_decoder_1_a_2, n4_7_decoder_1_b_2, n4_7_decoder_1_c_2,
       n4_7_decoder_1_d_2, n4_7_decoder_1_e, n4_7_decoder_1_f, n4_7_decoder_1_g, n4_7_decoder_2_a_2,
       n4_7_decoder_2_b_2, n4_7_decoder_2_c_2, n4_7_decoder_2_d_2, n4_7_decoder_2_e, n4_7_decoder_2_f,
       n4_7_decoder_2_g, ROJO_2_s1, ROJO_2_s2, ROJO_2_s3, ROJO_3_s1, ROJO_3_s2, ROJO_3_s3, ROJO_s1, ROJO_s2,
       ROJO_s3, sumador_4_bits_1_cout, sumador_4_bits_1_s0, sumador_4_bits_1_s1, sumador_4_bits_1_s2,
       sumador_4_bits_1_s3, sumador_4_bits_2_cout, sumador_4_bits_2_s0, sumador_4_bits_2_s1,
       sumador_4_bits_2_s2, sumador_4_bits_2_s3, sumador_con_acarreo_1_cout, sumador_con_acarreo_1_s0,
       sumador_con_acarreo_1_s1, sumador_con_acarreo_1_s2, sumador_con_acarreo_2_cout,
       sumador_con_acarreo_2_s0, sumador_con_acarreo_2_s1, sumador_con_acarreo_2_s2;

  CODIFICADOR_SIMPLIFICADO AZUL (
    .E(in_3), .D(in_4), .C(in_5), .B(in_6), .A(in_7), .S1(AZUL_s1), .S2(AZUL_s2), .S3(AZUL_s3));
  CODIFICADOR_SIMPLIFICADO ROJO (
    .E(in_8), .D(in_9), .C(in_10), .B(in_11), .A(in_12), .S1(ROJO_s1), .S2(ROJO_s2), .S3(ROJO_s3));
  CODIFICADOR_SIMPLIFICADO AZUL_2 (
    .E(in_13), .D(in_14), .C(in_15), .B(in_16), .A(in_17), .S1(AZUL_2_s1), .S2(AZUL_2_s2), .S3(AZUL_2_s3));
  CODIFICADOR_SIMPLIFICADO ROJO_2 (
    .E(in_18), .D(in_19), .C(in_20), .B(in_21), .A(in_22), .S1(ROJO_2_s1), .S2(ROJO_2_s2), .S3(ROJO_2_s3));
  CODIFICADOR_SIMPLIFICADO AZUL_3 (
    .E(in_23), .D(in_24), .C(in_25), .B(in_26), .A(in_27), .S1(AZUL_3_s1), .S2(AZUL_3_s2), .S3(AZUL_3_s3));
  CODIFICADOR_SIMPLIFICADO ROJO_3 (
    .E(in_28), .D(in_29), .C(in_30), .B(in_31), .A(in_32), .S1(ROJO_3_s1), .S2(ROJO_3_s2), .S3(ROJO_3_s3));
  SUMADOR_CON_ACARREO sumador_con_acarreo_1 (
    .Cin(1'b0), .A0(AZUL_s1), .B0(AZUL_2_s1), .A1(AZUL_s2), .B1(AZUL_2_s2), .A2(AZUL_s3), .B2(AZUL_2_s3),
    .S0(sumador_con_acarreo_1_s0), .S1(sumador_con_acarreo_1_s1), .S2(sumador_con_acarreo_1_s2),
    .Cout(sumador_con_acarreo_1_cout));
  SUMADOR_CON_ACARREO sumador_con_acarreo_2 (
    .Cin(1'b0), .A0(ROJO_s1), .B0(ROJO_2_s1), .A1(ROJO_s2), .B1(ROJO_2_s2), .A2(ROJO_s3), .B2(ROJO_2_s3),
    .S0(sumador_con_acarreo_2_s0), .S1(sumador_con_acarreo_2_s1), .S2(sumador_con_acarreo_2_s2),
    .Cout(sumador_con_acarreo_2_cout));
  sumador_4_bits sumador_4_bits_1 (
    .Cin(1'b0), .A0(sumador_con_acarreo_1_s0), .B0(AZUL_3_s1), .A1(sumador_con_acarreo_1_s1), .B1(AZUL_3_s2),
    .A2(sumador_con_acarreo_1_s2), .B2(AZUL_3_s3), .A3(sumador_con_acarreo_1_cout), .B3(1'b0),
    .S0(sumador_4_bits_1_s0), .S1(sumador_4_bits_1_s1), .S2(sumador_4_bits_1_s2), .S3(sumador_4_bits_1_s3),
    .Cout(sumador_4_bits_1_cout));
  sumador_4_bits sumador_4_bits_2 (
    .Cin(1'b0), .A0(sumador_con_acarreo_2_s0), .B0(ROJO_3_s1), .A1(sumador_con_acarreo_2_s1), .B1(ROJO_3_s2),
    .A2(sumador_con_acarreo_2_s2), .B2(ROJO_3_s3), .A3(sumador_con_acarreo_2_cout), .B3(1'b0),
    .S0(sumador_4_bits_2_s0), .S1(sumador_4_bits_2_s1), .S2(sumador_4_bits_2_s2), .S3(sumador_4_bits_2_s3),
    .Cout(sumador_4_bits_2_cout));
  Codificador_bin_BCD codificador_bin_bcd_1 (
    .B0(sumador_4_bits_1_s0), .B1(sumador_4_bits_1_s1), .B2(sumador_4_bits_1_s2), .B3(sumador_4_bits_1_s3),
    .C0(codificador_bin_bcd_1_c0), .C1(codificador_bin_bcd_1_c1), .C2(codificador_bin_bcd_1_c2),
    .C3(codificador_bin_bcd_1_c3), .C4(codificador_bin_bcd_1_c4));
  Codificador_bin_BCD codificador_bin_bcd_2 (
    .B0(sumador_4_bits_2_s0), .B1(sumador_4_bits_2_s1), .B2(sumador_4_bits_2_s2), .B3(sumador_4_bits_2_s3),
    .C0(codificador_bin_bcd_2_c0), .C1(codificador_bin_bcd_2_c1), .C2(codificador_bin_bcd_2_c2),
    .C3(codificador_bin_bcd_2_c3), .C4(codificador_bin_bcd_2_c4));
  comparador_4_bits comparador_4_bits_1 (
    .Concenso_A_B(in_1), .Concenso_A_B_2(in_2), .A0(sumador_4_bits_1_s0), .B0(sumador_4_bits_2_s0),
    .A1(sumador_4_bits_1_s1), .B1(sumador_4_bits_2_s1), .A2(sumador_4_bits_1_s2), .B2(sumador_4_bits_2_s2),
    .A3(sumador_4_bits_1_s3), .B3(sumador_4_bits_2_s3), .A_B(comparador_4_bits_1_a_b),
    .A_B_2(comparador_4_bits_1_a_b_2), .A_B_3(comparador_4_bits_1_a_b_3));
  LED led_1 (.in(comparador_4_bits_1_a_b));
  LED led_2 (.in(comparador_4_bits_1_a_b_2));
  LED led_3 (.in(comparador_4_bits_1_a_b_3));
  _4_7_decoder u_4_7_decoder_1 (
    .A(codificador_bin_bcd_1_c3), .B(codificador_bin_bcd_1_c2), .C(codificador_bin_bcd_1_c1),
    .D(codificador_bin_bcd_1_c0), .a_2(n4_7_decoder_1_a_2), .b_2(n4_7_decoder_1_b_2),
    .c_2(n4_7_decoder_1_c_2), .d_2(n4_7_decoder_1_d_2), .e(n4_7_decoder_1_e), .f(n4_7_decoder_1_f),
    .g(n4_7_decoder_1_g));
  _4_7_decoder u_4_7_decoder_2 (
    .A(codificador_bin_bcd_2_c3), .B(codificador_bin_bcd_2_c2), .C(codificador_bin_bcd_2_c1),
    .D(codificador_bin_bcd_2_c0), .a_2(n4_7_decoder_2_a_2), .b_2(n4_7_decoder_2_b_2),
    .c_2(n4_7_decoder_2_c_2), .d_2(n4_7_decoder_2_d_2), .e(n4_7_decoder_2_e), .f(n4_7_decoder_2_f),
    .g(n4_7_decoder_2_g));
  _7_Segment_Display u_7_segment_display_1 (
    .b(codificador_bin_bcd_1_c4), .c(codificador_bin_bcd_1_c4));  // open: g, f, a, e, d, dp
  _7_Segment_Display u_7_segment_display_2 (
    .b(codificador_bin_bcd_2_c4), .c(codificador_bin_bcd_2_c4));  // open: g, f, a, e, d, dp
  _7_Segment_Display u_7_segment_display_3 (
    .g(n4_7_decoder_1_g), .f(n4_7_decoder_1_f), .a(n4_7_decoder_1_a_2), .b(n4_7_decoder_1_b_2),
    .e(n4_7_decoder_1_e), .d(n4_7_decoder_1_d_2), .c(n4_7_decoder_1_c_2));  // open: dp
  _7_Segment_Display u_7_segment_display_4 (
    .g(n4_7_decoder_2_g), .f(n4_7_decoder_2_f), .a(n4_7_decoder_2_a_2), .b(n4_7_decoder_2_b_2),
    .e(n4_7_decoder_2_e), .d(n4_7_decoder_2_d_2), .c(n4_7_decoder_2_c_2));  // open: dp
  // also tied to GND on the sheet: {sumador_4_bits_1_cout, sumador_4_bits_2_cout}

  // Notes on the sheet:
  //   Concenso Ganador Esquina Azul
  //   Concenso Ganador Esquina Roja
  //   Esquina Azul
  //   Empate
  //   Esquina Roja
endmodule

module Codificador (
  output A,
  output S1,
  output B,
  output S2,
  output C,
  output D,
  output S3,
  output E
);

  wire and_1_out, and_2_out, and_3_out, and_4_out, not_1_out, not_2_out, not_3_out, not_4_out, not_5_out;

  not not_1 (not_1_out, A);
  not not_2 (not_2_out, A);
  not not_3 (not_3_out, A);
  not not_4 (not_4_out, C);
  not not_5 (not_5_out, A);
  and and_1 (and_1_out, not_1_out, C);
  and and_2 (and_2_out, not_2_out, B);
  and and_3 (and_3_out, not_3_out, not_4_out, D);
  and and_4 (and_4_out, not_5_out, B);
  or or_1 (S2, and_1_out, and_2_out);
  or or_2 (S3, and_3_out, and_4_out);

  assign S1 = A;
endmodule

// SUMADOR 4BITS
module Sumador (
  input  E1,
  input  E2,
  input  Cin,
  output S,
  output Cout
);

  wire and_1_out, and_2_out, and_3_out, and_4_out, and_5_out, and_6_out, and_7_out, not_1_out, not_2_out,
       not_3_out, not_4_out, not_5_out, not_6_out;

  not not_1 (not_1_out, E1);
  not not_2 (not_2_out, E2);
  not not_3 (not_3_out, E1);
  not not_4 (not_4_out, Cin);
  not not_5 (not_5_out, E2);
  not not_6 (not_6_out, Cin);
  and and_1 (and_1_out, E2, Cin);
  and and_2 (and_2_out, E1, Cin);
  and and_3 (and_3_out, E1, E2);
  and and_4 (and_4_out, not_1_out, not_2_out, Cin);
  and and_5 (and_5_out, not_3_out, E2, not_4_out);
  and and_6 (and_6_out, E1, not_5_out, not_6_out);
  and and_7 (and_7_out, E1, E2, Cin);
  or or_1 (Cout, and_1_out, and_2_out, and_3_out);
  or or_2 (S, and_4_out, and_5_out, and_6_out, and_7_out);
endmodule

module unidad_codificador (
  input  in_1,
  input  in_2,
  input  in_3,
  input  in_4,
  input  in_5,
  input  in_6,
  input  in_7,
  input  in_8,
  input  in_9,
  input  in_10,
  output out_11,
  output out_12,
  output out_13,
  output out_14,
  output out_15,
  output out_16
);

  Codificador codificador_1 (.A(in_2), .B(in_5), .C(in_1), .D(in_3), .E(in_4), .S1(out_11), .S2(out_12), .S3(out_13));
  Codificador codificador_2 (.A(in_6), .B(in_7), .C(in_8), .D(in_10), .E(in_9), .S1(out_14), .S2(out_15), .S3(out_16));
endmodule

module SUMADOR_SIMPLIFICADO (
  input  A0,
  input  B0,
  input  A1,
  input  B1,
  input  A2,
  input  B2,
  output S0,
  output S1,
  output S2,
  output Cout
);

  wire and_1_out, and_2_out, and_3_out, and_4_out, and_5_out, or_1_out, xor_2_out, xor_3_out;

  xor xor_1 (S0, A0, B0);
  and and_1 (and_1_out, A0, B0);
  xor xor_2 (xor_2_out, A1, B1);
  and and_2 (and_2_out, A1, B1);
  xor xor_3 (xor_3_out, A2, B2);
  and and_3 (and_3_out, A2, B2);
  and and_4 (and_4_out, and_1_out, xor_2_out);
  xor xor_4 (S1, and_1_out, xor_2_out);
  or or_1 (or_1_out, and_4_out, and_2_out);
  xor xor_5 (S2, or_1_out, xor_3_out);
  and and_5 (and_5_out, or_1_out, xor_3_out);
  or or_2 (Cout, and_5_out, and_3_out);
endmodule

// Cod BCD_BIN
module Codificador_bin_BCD (
  input  B0,
  input  B1,
  input  B2,
  input  B3,
  output C0,
  output C1,
  output C2,
  output C3,
  output C4
);

  wire and_1_out, and_2_out, not_1_out, not_2_out, not_3_out, not_4_out, not_5_out, or_1_out, or_2_out;

  not not_1 (not_1_out, B3);
  not not_2 (not_2_out, B1);
  not not_3 (not_3_out, B3);
  or or_1 (or_1_out, B2, B1);
  and and_1 (and_1_out, B1, not_1_out);
  and and_2 (and_2_out, not_2_out, B2, B3);
  or or_2 (or_2_out, not_3_out, B1);
  not not_4 (not_4_out, B1);
  and and_3 (C4, or_1_out, B3);
  or or_3 (C1, and_1_out, and_2_out);
  and and_4 (C2, B2, or_2_out);
  not not_5 (not_5_out, B2);
  and and_5 (C3, B3, not_5_out, not_4_out);

  assign C0 = B0;
endmodule

// CODEC
module CODIFICADOR_SIMPLIFICADO (
  input  E,
  input  D,
  input  C,
  input  B,
  input  A,
  output S1,
  output S2,
  output S3
);

  wire and_1_out, not_1_out, not_2_out, not_3_out, or_1_out, or_2_out;

  not not_1 (not_1_out, C);
  and and_1 (and_1_out, D, not_1_out);
  not not_2 (not_2_out, A);
  or or_1 (or_1_out, C, B);
  not not_3 (not_3_out, A);
  or or_2 (or_2_out, and_1_out, B);
  and and_2 (S2, not_2_out, or_1_out);
  and and_3 (S1, not_3_out, or_2_out);

  assign S3 = A;
endmodule

// SUM 4 BITS
module sumador_4_bits (
  input  Cin,
  input  A0,
  input  B0,
  input  A1,
  input  B1,
  input  A2,
  input  B2,
  input  A3,
  input  B3,
  output S0,
  output S1,
  output S2,
  output S3,
  output Cout
);

  wire and_1_out, and_2_out, and_3_out, and_4_out, and_5_out, and_6_out, and_7_out, and_8_out, or_1_out,
       or_2_out, or_3_out, xor_1_out, xor_2_out, xor_3_out, xor_4_out;

  xor xor_1 (xor_1_out, A0, B0);
  and and_1 (and_1_out, A0, B0);
  xor xor_2 (xor_2_out, A1, B1);
  and and_2 (and_2_out, A1, B1);
  xor xor_3 (xor_3_out, A2, B2);
  and and_3 (and_3_out, A2, B2);
  xor xor_4 (xor_4_out, A3, B3);
  and and_4 (and_4_out, A3, B3);
  and and_5 (and_5_out, or_2_out, xor_2_out);
  xor xor_5 (S0, Cin, xor_1_out);
  and and_6 (and_6_out, Cin, xor_1_out);
  xor xor_6 (S1, or_2_out, xor_2_out);
  or or_1 (or_1_out, and_5_out, and_2_out);
  xor xor_7 (S2, or_1_out, xor_3_out);
  and and_7 (and_7_out, or_1_out, xor_3_out);
  xor xor_8 (S3, or_3_out, xor_4_out);
  and and_8 (and_8_out, or_3_out, xor_4_out);
  or or_2 (or_2_out, and_6_out, and_1_out);
  or or_3 (or_3_out, and_7_out, and_3_out);
  or or_4 (Cout, and_8_out, and_4_out);
endmodule

// SUM 3 BITS
module SUMADOR_CON_ACARREO (
  input  Cin,
  input  A0,
  input  B0,
  input  A1,
  input  B1,
  input  A2,
  input  B2,
  output S0,
  output S1,
  output S2,
  output Cout
);

  wire and_1_out, and_2_out, and_3_out, and_4_out, and_5_out, and_6_out, or_1_out, or_2_out, xor_1_out,
       xor_2_out, xor_3_out;

  xor xor_1 (xor_1_out, A0, B0);
  and and_1 (and_1_out, A0, B0);
  xor xor_2 (xor_2_out, A1, B1);
  and and_2 (and_2_out, A1, B1);
  xor xor_3 (xor_3_out, A2, B2);
  and and_3 (and_3_out, A2, B2);
  and and_4 (and_4_out, or_2_out, xor_2_out);
  xor xor_4 (S0, Cin, xor_1_out);
  and and_5 (and_5_out, Cin, xor_1_out);
  xor xor_5 (S1, or_2_out, xor_2_out);
  or or_1 (or_1_out, and_4_out, and_2_out);
  xor xor_6 (S2, or_1_out, xor_3_out);
  and and_6 (and_6_out, or_1_out, xor_3_out);
  or or_2 (or_2_out, and_5_out, and_1_out);
  or or_3 (Cout, and_6_out, and_3_out);
endmodule

// COMPARADOR
module comparador_4_bits (
  input  Concenso_A_B,
  input  Concenso_A_B_2,
  input  A0,
  input  B0,
  input  A1,
  input  B1,
  input  A2,
  input  B2,
  input  A3,
  input  B3,
  output A_B,
  output A_B_2,
  output A_B_3
);

  wire and_1_out, and_2_out, and_3_out, and_4_out, and_5_out, and_6_out, and_7_out, and_8_out, and_9_out,
       not_1_out, not_2_out, not_3_out, not_4_out, not_5_out, not_6_out, not_7_out, not_8_out, not_9_out,
       not_10_out, xnor_1_out, xnor_2_out, xnor_3_out, xnor_4_out;

  xnor xnor_1 (xnor_1_out, A0, B0);
  xnor xnor_2 (xnor_2_out, A1, B1);
  not not_1 (not_1_out, A1);
  xnor xnor_3 (xnor_3_out, A3, B3);
  not not_2 (not_2_out, B0);
  not not_3 (not_3_out, A0);
  xnor xnor_4 (xnor_4_out, A2, B2);
  not not_4 (not_4_out, B1);
  not not_5 (not_5_out, B2);
  not not_6 (not_6_out, A2);
  not not_7 (not_7_out, B3);
  not not_8 (not_8_out, A3);
  and and_1 (and_1_out, A0, xnor_4_out, xnor_2_out, xnor_3_out, not_2_out);
  and and_2 (and_2_out, A1, xnor_3_out, xnor_4_out, not_4_out);
  and and_3 (and_3_out, xnor_1_out, xnor_3_out, xnor_4_out, xnor_2_out);
  and and_4 (and_4_out, not_1_out, xnor_3_out, xnor_4_out, B1);
  and and_5 (and_5_out, not_3_out, xnor_3_out, xnor_2_out, xnor_4_out, B0);
  and and_6 (and_6_out, A2, xnor_3_out, not_5_out);
  and and_7 (and_7_out, not_6_out, xnor_3_out, B2);
  and and_8 (and_8_out, A3, not_7_out);
  and and_9 (and_9_out, not_8_out, B3);
  not not_9 (not_9_out, Concenso_A_B);
  not not_10 (not_10_out, Concenso_A_B_2);
  or or_1 (A_B, and_1_out, and_8_out, Concenso_A_B, and_6_out, and_2_out);
  and and_10 (A_B_2, not_9_out, and_3_out, not_10_out);
  or or_2 (A_B_3, and_4_out, Concenso_A_B_2, and_7_out, and_9_out, and_5_out);
endmodule

// A B C D
module _4_7_decoder (
  input  A,
  input  B,
  input  C,
  input  D,
  output a_2,
  output b_2,
  output c_2,
  output d_2,
  output e,
  output f,
  output g
);

  wire and_1_out, and_2_out, and_3_out, and_4_out, and_5_out, and_6_out, and_7_out, and_8_out, and_9_out,
       and_10_out, and_11_out, and_12_out, and_13_out, and_14_out, and_15_out, and_16_out, not_1_out,
       not_2_out, not_3_out, not_4_out, not_5_out, not_6_out, not_7_out, not_8_out, not_9_out, not_10_out,
       not_11_out, not_12_out, not_13_out, not_14_out, not_15_out, not_16_out, not_17_out, not_18_out,
       not_19_out, not_20_out, not_21_out;

  and and_1 (and_1_out, B, D);
  not not_1 (not_1_out, B);
  and and_2 (and_2_out, not_1_out, not_2_out);
  not not_2 (not_2_out, D);
  not not_3 (not_3_out, B);
  not not_4 (not_4_out, C);
  and and_3 (and_3_out, not_4_out, not_5_out);
  not not_5 (not_5_out, D);
  and and_4 (and_4_out, C, D);
  or or_1 (c_2, B, not_6_out, D);
  not not_6 (not_6_out, C);
  not not_7 (not_7_out, B);
  and and_5 (and_5_out, not_7_out, not_8_out);
  not not_8 (not_8_out, D);
  not not_9 (not_9_out, B);
  and and_6 (and_6_out, not_9_out, C);
  and and_7 (and_7_out, C, not_10_out);
  not not_10 (not_10_out, D);
  and and_8 (and_8_out, B, not_11_out, D);
  not not_11 (not_11_out, C);
  not not_12 (not_12_out, B);
  and and_9 (and_9_out, not_12_out, not_13_out);
  not not_13 (not_13_out, D);
  and and_10 (and_10_out, C, not_14_out);
  not not_14 (not_14_out, D);
  and and_11 (and_11_out, B, not_15_out);
  not not_15 (not_15_out, C);
  and and_12 (and_12_out, B, not_16_out);
  not not_16 (not_16_out, D);
  not not_17 (not_17_out, C);
  and and_13 (and_13_out, not_17_out, not_18_out);
  not not_18 (not_18_out, D);
  and and_14 (and_14_out, B, not_19_out);
  not not_19 (not_19_out, C);
  not not_20 (not_20_out, B);
  and and_15 (and_15_out, not_20_out, C);
  and and_16 (and_16_out, C, not_21_out);
  not not_21 (not_21_out, D);
  or or_2 (a_2, A, C, and_1_out, and_2_out);
  or or_3 (b_2, not_3_out, and_3_out, and_4_out);
  or or_4 (d_2, A, and_5_out, and_6_out, and_7_out, and_8_out);
  or or_5 (e, and_9_out, and_10_out);
  or or_6 (f, A, and_11_out, and_12_out, and_13_out);
  or or_7 (g, A, and_14_out, and_15_out, and_16_out);
endmodule
