// Logisim project UC3_Semaforo.circ as structural Verilog
module CONTADOR_12 (
);

  wire and_1_out, and_2_out, and_3_out, button_1_out, button_2_out, clock_1_out, cont_5_0_desc_1_lsb,
       cont_5_0_desc_1_msb, cont_5_0_desc_1_out_4, D0_q, D1_q, D2_q, D3_q, d_ff_1_q, d_ff_2_q, d_ff_3_q,
       d_ff_3_qn, decoder_display_decenas_a, decoder_display_decenas_b, decoder_display_decenas_c,
       decoder_display_decenas_d, decoder_display_decenas_e, decoder_display_decenas_f,
       decoder_display_decenas_g, decoder_display_uds_a, decoder_display_uds_b, decoder_display_uds_c,
       decoder_display_uds_d, decoder_display_uds_e, decoder_display_uds_f, decoder_display_uds_g,
       flipflop_d0_cont_12_1_d0, flipflop_d1_cont_12_1_d1, flipflop_d2_cont_12_1_d2,
       flipflop_d3_cont_12_1_d3, n4_7_decoder_cont5_1_a_2, n4_7_decoder_cont5_1_b_2,
       n4_7_decoder_cont5_1_c_2, n4_7_decoder_cont5_1_d_2, n4_7_decoder_cont5_1_e, n4_7_decoder_cont5_1_f,
       n4_7_decoder_cont5_1_g, nor_1_out, not_1_out, or_1_out, or_2_out, or_3_out, sumador_4_bits_1_cout,
       sumador_4_bits_1_s0, sumador_4_bits_1_s1, sumador_4_bits_1_s2, sumador_4_bits_1_s3;

  D_Flip_Flop d_ff_1 (
    .clk(d_ff_3_qn), .D(nor_1_out), .Q(d_ff_1_q), .preset(d_ff_2_q), .reset(d_ff_2_q));  // open: Qn, en
  Clock clock_1 (.out(clock_1_out));
  nor nor_1 (nor_1_out, cont_5_0_desc_1_lsb, cont_5_0_desc_1_out_4, cont_5_0_desc_1_msb);
  FLIPFLOP_D3_cont_12 flipflop_d3_cont_12_1 (.Q3(D3_q), .Q2(D2_q), .Q1(D1_q), .Q0(D0_q), .D3(flipflop_d3_cont_12_1_d3));
  D_Flip_Flop D3 (
    .clk(clock_1_out), .D(flipflop_d3_cont_12_1_d3), .Q(D3_q), .preset(button_1_out), .en(d_ff_1_q),
    .reset(button_1_out));  // open: Qn
  D_Flip_Flop d_ff_2 (
    .clk(not_1_out), .D(not_1_out), .Q(d_ff_2_q), .preset(button_2_out), .reset(button_2_out));  // open: Qn, en
  FLIPFLOP_D2_cont_12 flipflop_d2_cont_12_1 (.Q3(D3_q), .Q2(D2_q), .Q1(D1_q), .Q0(D0_q), .D2(flipflop_d2_cont_12_1_d2));
  D_Flip_Flop D2 (
    .clk(clock_1_out), .D(flipflop_d2_cont_12_1_d2), .Q(D2_q), .preset(button_1_out), .en(d_ff_1_q),
    .reset(button_1_out));  // open: Qn
  FLIPFLOP_D1_cont_12 flipflop_d1_cont_12_1 (.Q3(D3_q), .Q2(D2_q), .Q1(D1_q), .Q0(D0_q), .D1(flipflop_d1_cont_12_1_d1));
  D_Flip_Flop D1 (
    .clk(clock_1_out), .D(flipflop_d1_cont_12_1_d1), .Q(D1_q), .preset(button_1_out), .en(d_ff_1_q),
    .reset(button_1_out));  // open: Qn
  FLIPFLOP_D0_cont_12 flipflop_d0_cont_12_1 (.Q3(D3_q), .Q2(D2_q), .Q1(D1_q), .Q0(D0_q), .D0(flipflop_d0_cont_12_1_d0));
  D_Flip_Flop D0 (
    .clk(clock_1_out), .D(flipflop_d0_cont_12_1_d0), .Q(D0_q), .preset(button_1_out), .en(d_ff_1_q),
    .reset(button_1_out));  // open: Qn
  and and_1 (and_1_out, D3_q, D2_q);
  and and_2 (and_2_out, D3_q, D1_q);
  Button button_1 (.out(button_1_out));
  Button button_2 (.out(button_2_out));
  or or_1 (or_1_out, and_1_out, and_2_out);
  or or_2 (or_2_out, D3_q, D2_q, D1_q, D0_q);
  D_Flip_Flop d_ff_3 (
    .clk(nor_1_out), .D(button_2_out), .Q(d_ff_3_q), .Qn(d_ff_3_qn), .preset(button_2_out));  // open: en, reset
  _4_7_DECODER decoder_display_decenas (
    .Q3(1'b0), .Q2(1'b0), .Q1(1'b0), .Q0(or_1_out), .a(decoder_display_decenas_a),
    .b(decoder_display_decenas_b), .c(decoder_display_decenas_c), .d(decoder_display_decenas_d),
    .e(decoder_display_decenas_e), .f(decoder_display_decenas_f), .g(decoder_display_decenas_g));
  sumador_4_bits sumador_4_bits_1 (
    .Cin(1'b0), .A0(D0_q), .B0(1'b0), .A1(D1_q), .B1(or_1_out), .A2(D2_q), .B2(or_1_out), .A3(D3_q),
    .B3(1'b0), .S0(sumador_4_bits_1_s0), .S1(sumador_4_bits_1_s1), .S2(sumador_4_bits_1_s2),
    .S3(sumador_4_bits_1_s3), .Cout(sumador_4_bits_1_cout));
  _4_7_DECODER decoder_display_uds (
    .Q3(sumador_4_bits_1_s3), .Q2(sumador_4_bits_1_s2), .Q1(sumador_4_bits_1_s1), .Q0(sumador_4_bits_1_s0),
    .a(decoder_display_uds_a), .b(decoder_display_uds_b), .c(decoder_display_uds_c),
    .d(decoder_display_uds_d), .e(decoder_display_uds_e), .f(decoder_display_uds_f), .g(decoder_display_uds_g));
  cont_5_0_desc cont_5_0_desc_1 (
    .CLK(clock_1_out), .ENABLE(d_ff_3_q), .MSB(cont_5_0_desc_1_msb), .out_4(cont_5_0_desc_1_out_4),
    .LSB(cont_5_0_desc_1_lsb));
  _7_Segment_Display u_7_segment_display_1 (
    .g(decoder_display_decenas_g), .f(decoder_display_decenas_f), .a(decoder_display_decenas_a),
    .b(decoder_display_decenas_b), .e(decoder_display_decenas_e), .d(decoder_display_decenas_d),
    .c(decoder_display_decenas_c), .dp(1'b0));
  not not_1 (not_1_out, or_2_out);
  _7_Segment_Display u_7_segment_display_2 (
    .g(decoder_display_uds_g), .f(decoder_display_uds_f), .a(decoder_display_uds_a),
    .b(decoder_display_uds_b), .e(decoder_display_uds_e), .d(decoder_display_uds_d),
    .c(decoder_display_uds_c), .dp(1'b0));
  _4_7_decoder_cont5 u_4_7_decoder_cont5_1 (
    .A(1'b0), .B(cont_5_0_desc_1_lsb), .C(cont_5_0_desc_1_out_4), .D(cont_5_0_desc_1_msb),
    .a_2(n4_7_decoder_cont5_1_a_2), .b_2(n4_7_decoder_cont5_1_b_2), .c_2(n4_7_decoder_cont5_1_c_2),
    .d_2(n4_7_decoder_cont5_1_d_2), .e(n4_7_decoder_cont5_1_e), .f(n4_7_decoder_cont5_1_f),
    .g(n4_7_decoder_cont5_1_g));
  _7_Segment_Display u_7_segment_display_3 (
    .g(n4_7_decoder_cont5_1_g), .f(n4_7_decoder_cont5_1_f), .a(n4_7_decoder_cont5_1_a_2),
    .b(n4_7_decoder_cont5_1_b_2), .e(n4_7_decoder_cont5_1_e), .d(n4_7_decoder_cont5_1_d_2),
    .c(n4_7_decoder_cont5_1_c_2));  // open: dp
  LED led_1 (.in(or_2_out));
  and and_3 (and_3_out, not_1_out, nor_1_out);
  LED led_2 (.in(d_ff_3_q));
  LED led_3 (.in(and_3_out));
  LED led_4 (.in(or_3_out));
  LED led_5 (.in(or_2_out));
  or or_3 (or_3_out, and_3_out, d_ff_3_q);
  // also tied to GND on the sheet: sumador_4_bits_1_cout

  // Notes on the sheet:
  //   PULSADOR PEATON
  //   Q1
  //   Q2
  //   Q0
  //   Q3
  //   SEMAFOROS DE LOS COCHES
  //   SEMAFORO DE PEATON
endmodule

// D3
module FLIPFLOP_D3_cont_12 (
  input  Q3,
  input  Q2,
  input  Q1,
  input  Q0,
  output D3
);

  wire and_1_out, and_2_out, and_3_out, and_4_out, not_1_out, not_2_out, not_3_out, not_4_out, not_5_out,
       not_6_out, not_7_out, not_8_out;

  not not_1 (not_1_out, Q3);
  not not_2 (not_2_out, Q2);
  not not_3 (not_3_out, Q1);
  not not_4 (not_4_out, Q0);
  not not_5 (not_5_out, Q1);
  not not_6 (not_6_out, Q0);
  not not_7 (not_7_out, Q2);
  not not_8 (not_8_out, Q2);
  and and_1 (and_1_out, not_1_out, not_2_out, not_3_out, not_4_out);
  and and_2 (and_2_out, Q3, Q2, not_5_out, not_6_out);
  and and_3 (and_3_out, Q3, not_7_out, Q0);
  and and_4 (and_4_out, Q3, not_8_out, Q1);
  or or_1 (D3, and_1_out, and_2_out, and_3_out, and_4_out);
endmodule

// D2
module FLIPFLOP_D2_cont_12 (
  input  Q3,
  input  Q2,
  input  Q1,
  input  Q0,
  output D2
);

  wire and_1_out, and_2_out, and_3_out, not_1_out, not_2_out, not_3_out, not_4_out, not_5_out;

  not not_1 (not_1_out, Q2);
  not not_2 (not_2_out, Q1);
  and and_1 (and_1_out, not_1_out, not_2_out, not_3_out);
  not not_3 (not_3_out, Q0);
  not not_4 (not_4_out, Q3);
  and and_2 (and_2_out, not_4_out, Q2, Q0);
  not not_5 (not_5_out, Q3);
  and and_3 (and_3_out, not_5_out, Q2, Q1);
  or or_1 (D2, and_1_out, and_2_out, and_3_out);
endmodule

// D1
module FLIPFLOP_D1_cont_12 (
  input  Q3,
  input  Q2,
  input  Q1,
  input  Q0,
  output D1
);

  wire and_1_out, and_2_out, and_3_out, and_4_out, not_1_out, not_2_out, not_3_out, not_4_out, not_5_out,
       not_6_out;

  and and_1 (and_1_out, Q2, not_1_out, not_2_out);
  not not_1 (not_1_out, Q1);
  not not_2 (not_2_out, Q0);
  not not_3 (not_3_out, Q1);
  and and_2 (and_2_out, Q3, not_3_out, not_4_out);
  not not_4 (not_4_out, Q0);
  not not_5 (not_5_out, Q2);
  and and_3 (and_3_out, not_5_out, Q1, Q0);
  not not_6 (not_6_out, Q3);
  and and_4 (and_4_out, not_6_out, Q1, Q0);
  or or_1 (D1, and_1_out, and_2_out, and_3_out, and_4_out);
endmodule

module FLIPFLOP_D0_cont_12 (
  input  Q3,
  input  Q2,
  input  Q1,
  input  Q0,
  output D0
);

  wire and_1_out, and_2_out, and_3_out, not_1_out, not_2_out, not_3_out, not_4_out, not_5_out, not_6_out;

  not not_1 (not_1_out, Q2);
  and and_1 (and_1_out, not_1_out, Q1, not_2_out);
  not not_2 (not_2_out, Q0);
  not not_3 (not_3_out, Q3);
  and and_2 (and_2_out, not_3_out, Q2, not_4_out);
  not not_4 (not_4_out, Q0);
  and and_3 (and_3_out, Q3, not_5_out, not_6_out);
  not not_5 (not_5_out, Q1);
  not not_6 (not_6_out, Q0);
  or or_1 (D0, and_1_out, and_2_out, and_3_out);
endmodule

module _4_7_DECODER (
  input  Q3,
  input  Q2,
  input  Q1,
  input  Q0,
  output a,
  output b,
  output c,
  output d,
  output e,
  output f,
  output g
);

  wire and_1_out, and_2_out, and_3_out, and_4_out, and_5_out, and_6_out, and_7_out, and_8_out, and_9_out,
       and_10_out, and_11_out, and_12_out, and_13_out, and_14_out, and_15_out, and_16_out, not_1_out,
       not_2_out, not_3_out, not_4_out, not_5_out, not_6_out, not_7_out, not_8_out, not_9_out, not_10_out,
       not_11_out, not_12_out, not_13_out, not_14_out, not_15_out, not_16_out, not_17_out, not_18_out,
       not_19_out, not_20_out, not_21_out;

  and and_1 (and_1_out, Q2, Q0);
  not not_1 (not_1_out, Q2);
  and and_2 (and_2_out, not_1_out, not_2_out);
  not not_2 (not_2_out, Q0);
  not not_3 (not_3_out, Q2);
  not not_4 (not_4_out, Q1);
  and and_3 (and_3_out, not_4_out, not_5_out);
  not not_5 (not_5_out, Q0);
  and and_4 (and_4_out, Q1, Q0);
  not not_6 (not_6_out, Q1);
  or or_1 (c, Q2, not_6_out, Q0);
  not not_7 (not_7_out, Q2);
  and and_5 (and_5_out, not_7_out, not_8_out);
  not not_8 (not_8_out, Q0);
  not not_9 (not_9_out, Q2);
  and and_6 (and_6_out, not_9_out, Q1);
  and and_7 (and_7_out, Q1, not_10_out);
  not not_10 (not_10_out, Q0);
  and and_8 (and_8_out, Q2, not_11_out, Q0);
  not not_11 (not_11_out, Q1);
  not not_12 (not_12_out, Q2);
  and and_9 (and_9_out, not_12_out, not_13_out);
  not not_13 (not_13_out, Q0);
  and and_10 (and_10_out, Q1, not_14_out);
  not not_14 (not_14_out, Q0);
  and and_11 (and_11_out, Q2, not_15_out);
  not not_15 (not_15_out, Q1);
  and and_12 (and_12_out, Q2, not_16_out);
  not not_16 (not_16_out, Q0);
  not not_17 (not_17_out, Q1);
  and and_13 (and_13_out, not_17_out, not_18_out);
  not not_18 (not_18_out, Q0);
  and and_14 (and_14_out, Q2, not_19_out);
  not not_19 (not_19_out, Q1);
  not not_20 (not_20_out, Q2);
  and and_15 (and_15_out, not_20_out, Q1);
  and and_16 (and_16_out, Q1, not_21_out);
  not not_21 (not_21_out, Q0);
  or or_2 (a, Q3, Q1, and_1_out, and_2_out);
  or or_3 (b, not_3_out, and_3_out, and_4_out);
  or or_4 (d, Q3, and_5_out, and_6_out, and_7_out, and_8_out);
  or or_5 (e, and_9_out, and_10_out);
  or or_6 (f, Q3, and_11_out, and_12_out, and_13_out);
  or or_7 (g, Q3, and_14_out, and_15_out, and_16_out);
endmodule

module sumador_4_bits (
  input  Cin,
  input  A0,
  input  B0,
  input  A1,
  input  B1,
  input  A2,
  input  B2,
  input  A3,
  input  B3,
  output S0,
  output S1,
  output S2,
  output S3,
  output Cout
);

  wire and_1_out, and_2_out, and_3_out, and_4_out, and_5_out, and_6_out, and_7_out, and_8_out, or_1_out,
       or_2_out, or_3_out, xor_1_out, xor_2_out, xor_3_out, xor_4_out;

  xor xor_1 (xor_1_out, A0, B0);
  and and_1 (and_1_out, A0, B0);
  xor xor_2 (xor_2_out, A1, B1);
  and and_2 (and_2_out, A1, B1);
  xor xor_3 (xor_3_out, A2, B2);
  and and_3 (and_3_out, A2, B2);
  xor xor_4 (xor_4_out, A3, B3);
  and and_4 (and_4_out, A3, B3);
  and and_5 (and_5_out, or_2_out, xor_2_out);
  xor xor_5 (S0, Cin, xor_1_out);
  and and_6 (and_6_out, Cin, xor_1_out);
  xor xor_6 (S1, or_2_out, xor_2_out);
  or or_1 (or_1_out, and_5_out, and_2_out);
  xor xor_7 (S2, or_1_out, xor_3_out);
  and and_7 (and_7_out, or_1_out, xor_3_out);
  xor xor_8 (S3, or_3_out, xor_4_out);
  and and_8 (and_8_out, or_3_out, xor_4_out);
  or or_2 (or_2_out, and_6_out, and_1_out);
  or or_3 (or_3_out, and_7_out, and_3_out);
  or or_4 (Cout, and_8_out, and_4_out);
endmodule

module _4_7_decoder_cont5 (
  input  A,
  input  B,
  input  C,
  input  D,
  output a_2,
  output b_2,
  output c_2,
  output d_2,
  output e,
  output f,
  output g
);

  wire and_1_out, and_2_out, and_3_out, and_4_out, and_5_out, and_6_out, and_7_out, and_8_out, and_9_out,
       and_10_out, and_11_out, and_12_out, and_13_out, and_14_out, and_15_out, and_16_out, not_1_out,
       not_2_out, not_3_out, not_4_out, not_5_out, not_6_out, not_7_out, not_8_out, not_9_out, not_10_out,
       not_11_out, not_12_out, not_13_out, not_14_out, not_15_out, not_16_out, not_17_out, not_18_out,
       not_19_out, not_20_out, not_21_out;

  and and_1 (and_1_out, B, D);
  not not_1 (not_1_out, B);
  and and_2 (and_2_out, not_1_out, not_2_out);
  not not_2 (not_2_out, D);
  not not_3 (not_3_out, B);
  not not_4 (not_4_out, C);
  and and_3 (and_3_out, not_4_out, not_5_out);
  not not_5 (not_5_out, D);
  and and_4 (and_4_out, C, D);
  not not_6 (not_6_out, C);
  or or_1 (c_2, B, not_6_out, D);
  not not_7 (not_7_out, B);
  and and_5 (and_5_out, not_7_out, not_8_out);
  not not_8 (not_8_out, D);
  not not_9 (not_9_out, B);
  and and_6 (and_6_out, not_9_out, C);
  and and_7 (and_7_out, C, not_10_out);
  not not_10 (not_10_out, D);
  not not_11 (not_11_out, C);
  and and_8 (and_8_out, B, not_11_out, D);
  not not_12 (not_12_out, B);
  and and_9 (and_9_out, not_12_out, not_13_out);
  not not_13 (not_13_out, D);
  and and_10 (and_10_out, C, not_14_out);
  not not_14 (not_14_out, D);
  and and_11 (and_11_out, B, not_15_out);
  not not_15 (not_15_out, C);
  and and_12 (and_12_out, B, not_16_out);
  not not_16 (not_16_out, D);
  not not_17 (not_17_out, C);
  and and_13 (and_13_out, not_17_out, not_18_out);
  not not_18 (not_18_out, D);
  and and_14 (and_14_out, B, not_19_out);
  not not_19 (not_19_out, C);
  not not_20 (not_20_out, B);
  and and_15 (and_15_out, not_20_out, C);
  and and_16 (and_16_out, C, not_21_out);
  not not_21 (not_21_out, D);
  or or_2 (a_2, A, C, and_1_out, and_2_out);
  or or_3 (b_2, not_3_out, and_3_out, and_4_out);
  or or_4 (d_2, A, and_5_out, and_6_out, and_7_out, and_8_out);
  or or_5 (e, and_9_out, and_10_out);
  or or_6 (f, A, and_11_out, and_12_out, and_13_out);
  or or_7 (g, A, and_14_out, and_15_out, and_16_out);
endmodule

module cont_5_0_desc (
  input  CLK,
  input  ENABLE,
  output MSB,
  output out_4,
  output LSB
);

  wire and_1_out, d_ff_1_q, d_ff_1_qn, d_ff_2_q, d_ff_2_qn, d_ff_3_q, d_ff_3_qn, not_1_out, not_2_out,
       not_3_out, or_1_out;

  not not_1 (not_1_out, d_ff_1_q);
  and and_1 (and_1_out, not_1_out, d_ff_2_q, not_2_out);
  not not_2 (not_2_out, d_ff_3_q);
  D_Flip_Flop d_ff_1 (
    .clk(CLK), .D(d_ff_1_qn), .Q(d_ff_1_q), .Qn(d_ff_1_qn), .en(ENABLE), .reset(and_1_out));  // open: preset
  D_Flip_Flop d_ff_2 (
    .clk(d_ff_1_q), .D(d_ff_2_qn), .Q(d_ff_2_q), .Qn(d_ff_2_qn), .en(ENABLE), .reset(and_1_out));  // open: preset
  D_Flip_Flop d_ff_3 (
    .clk(d_ff_2_q), .D(d_ff_3_qn), .Q(d_ff_3_q), .Qn(d_ff_3_qn), .en(ENABLE), .reset(and_1_out));  // open: preset
  or or_1 (or_1_out, d_ff_3_q, d_ff_2_q);
  not not_3 (not_3_out, d_ff_2_q);
  and and_2 (MSB, or_1_out, d_ff_1_q);
  and and_3 (out_4, not_3_out, d_ff_3_q);
  and and_4 (LSB, d_ff_2_q, d_ff_3_q);
endmodule
