// Logisim project circuito.circ as structural Verilog
module main (
  input  A,
  input  B,
  input  C,
  input  D
);

  wire n4_to_7seg_1_a_2, n4_to_7seg_1_b_2, n4_to_7seg_1_c_2, n4_to_7seg_1_d_2, n4_to_7seg_1_e,
       n4_to_7seg_1_f, n4_to_7seg_1_g;

  _4_to_7seg u_4_to_7seg_1 (
    .A(A), .B(B), .C(C), .D(D), .a_2(n4_to_7seg_1_a_2), .b_2(n4_to_7seg_1_b_2), .c_2(n4_to_7seg_1_c_2),
    .d_2(n4_to_7seg_1_d_2), .e(n4_to_7seg_1_e), .f(n4_to_7seg_1_f), .g(n4_to_7seg_1_g));
  _7_Segment_Display u_7_segment_display_1 (
    .g(n4_to_7seg_1_g), .f(n4_to_7seg_1_f), .a(n4_to_7seg_1_a_2), .b(n4_to_7seg_1_b_2), .e(n4_to_7seg_1_e),
    .d(n4_to_7seg_1_d_2), .c(n4_to_7seg_1_c_2));  // open: dp
endmodule

module _4_to_7seg (
  input  A,
  input  B,
  input  C,
  input  D,
  output a_2,
  output b_2,
  output c_2,
  output d_2,
  output e,
  output f,
  output g
);

  wire and_1_out, and_2_out, and_3_out, and_4_out, and_5_out, and_6_out, and_7_out, and_8_out, and_9_out,
       and_10_out, and_11_out, and_12_out, not_1_out, not_2_out, not_3_out, not_4_out;

  not not_1 (not_1_out, A);
  not not_2 (not_2_out, B);
  not not_3 (not_3_out, C);
  not not_4 (not_4_out, D);
  and and_1 (and_1_out, A, not_4_out);
  and and_2 (and_2_out, not_2_out, not_4_out);
  and and_3 (and_3_out, C, not_4_out);
  and and_4 (and_4_out, not_1_out, not_3_out);
  and and_5 (and_5_out, not_1_out, B);
  and and_6 (and_6_out, not_2_out, A);
  and and_7 (and_7_out, not_2_out, not_1_out, not_4_out);
  and and_8 (and_8_out, B, C, not_4_out);
  and and_9 (and_9_out, not_4_out, not_3_out, A);
  and and_10 (and_10_out, not_4_out, not_2_out);
  and and_11 (and_11_out, not_4_out, B);
  and and_12 (and_12_out, not_4_out, not_3_out);
  or or_1 (a_2, and_1_out, and_2_out, and_3_out);
  or or_2 (b_2, not_2_out, and_4_out, D);
  or or_3 (c_2, and_4_out, and_5_out, and_6_out, D);
  or or_4 (d_2, and_7_out, and_8_out, and_9_out);
  or or_5 (e, and_1_out, and_10_out, and_3_out);
  or or_6 (f, and_1_out, and_11_out, and_12_out);
  or or_7 (g, and_6_out, and_5_out, C, D);
endmodule
